// Logisim project CPU.circ as structural Verilog: 3 circuits, main circuit implementation
module implementation (
  output [7:0] print_R0,
  output [7:0] print_R1,
  output halt
);

  wire ALU0, ALU1, and_3_out, and_4_out, and_5_out, and_6_out, CLK, comparator_1_eq, comparator_2_eq, DS,
       IRIN, IROUT, MARIN, MDROUT, not_1_out, not_2_out, not_3_out, OFFSET, ONE, PCIN, PCOUT, R0IN, R0OUT,
       R1IN, R1OUT, RDSIN, RDSOUT, READ, RSOUT, XIN, ZIN, Zout;
  wire [3:0] controlled_buffer_1_out, controlled_buffer_1_out_2;
  wire [3:3] and_2_out;
  wire [7:0] alu_1_z, bit_extender_1_out, bit_extender_2_out, IR, MAR_q, multiplexer_1_out, PC, ram_1_dout,
       register_1_q, X_REG_q;

  Register #(.trigger("high")) MAR (
    .D({controlled_buffer_1_out_2, controlled_buffer_1_out}), .en(MARIN), .clk(CLK), .Q(MAR_q));  // open: clr
  RAM ram_1 (.addr(MAR_q), .oe(READ), .clk(CLK), .dout(ram_1_dout));  // open: we, din
  Clock clock_1 (.out(CLK));
  Register PC_REG (
    .D({controlled_buffer_1_out_2, controlled_buffer_1_out}), .en(PCIN), .clk(CLK), .Q(PC));  // open: clr
  assign {controlled_buffer_1_out_2, controlled_buffer_1_out} = MDROUT ? ram_1_dout : 8'bz;  // Controlled_Buffer controlled_buffer_1
  Comparator comparator_1 (.a(PC), .b(8'hf), .eq(comparator_1_eq));  // open: gt, lt
  Comparator comparator_2 (.a({IR[7:4], DS, IR[2:0]}), .b({8{1'b0}}), .eq(comparator_2_eq));  // open: gt, lt
  assign {controlled_buffer_1_out_2, controlled_buffer_1_out} = PCOUT ? PC : 8'bz;  // Controlled_Buffer controlled_buffer_2
  Register #(.trigger("high")) IR_REG (
    .D({controlled_buffer_1_out_2, controlled_buffer_1_out}), .en(IRIN), .clk(CLK), .Q({IR[7:4], DS, IR[2:0]}));  // open: clr
  Multiplexer #(.enable("false"), .width(8)) multiplexer_1 (
    .in0({controlled_buffer_1_out_2, controlled_buffer_1_out}), .in1(bit_extender_1_out),
    .out(multiplexer_1_out), .sel(OFFSET));
  and and_1 (halt, comparator_1_eq, comparator_2_eq);
  assign {controlled_buffer_1_out_2, controlled_buffer_1_out} = IROUT ? bit_extender_2_out : 8'bz;  // Controlled_Buffer controlled_buffer_3
  assign bit_extender_1_out = {{4{controlled_buffer_1_out[3]}}, controlled_buffer_1_out};  // Bit_Extender bit_extender_1
  Register X_REG (
    .D({controlled_buffer_1_out_2, controlled_buffer_1_out}), .en(XIN), .clk(CLK), .Q(X_REG_q));  // open: clr
  and and_2 (and_2_out[3], DS, IR[7]);
  assign bit_extender_2_out = {{4{and_2_out[3]}}, {and_2_out[3], IR[2:0]}};  // Bit_Extender bit_extender_2
  Register R0_REG (
    .D({controlled_buffer_1_out_2, controlled_buffer_1_out}), .en(R0IN), .clk(CLK), .Q(print_R0));  // open: clr
  assign {controlled_buffer_1_out_2, controlled_buffer_1_out} = R0OUT ? print_R0 : 8'bz;  // Controlled_Buffer controlled_buffer_4
  ALU alu_1 (.A(X_REG_q), .B(multiplexer_1_out), .ALU0(ALU0), .ALU1(ALU1), .z(alu_1_z));
  not not_1 (not_1_out, DS);
  not not_2 (not_2_out, IR[2]);
  Register R1_REG (
    .D({controlled_buffer_1_out_2, controlled_buffer_1_out}), .en(R1IN), .clk(CLK), .Q(print_R1));  // open: clr
  Register register_1 (.D(alu_1_z), .en(ZIN), .clk(CLK), .Q(register_1_q));  // open: clr
  and and_3 (and_3_out, RDSOUT, DS);
  and and_4 (and_4_out, RSOUT, IR[2]);
  and and_5 (and_5_out, RDSOUT, not_1_out);
  and and_6 (and_6_out, RSOUT, not_2_out);
  assign {controlled_buffer_1_out_2, controlled_buffer_1_out} = R1OUT ? print_R1 : 8'bz;  // Controlled_Buffer controlled_buffer_5
  assign {controlled_buffer_1_out_2, controlled_buffer_1_out} = Zout ? register_1_q : 8'bz;  // Controlled_Buffer controlled_buffer_6
  not not_3 (not_3_out, DS);
  and and_7 (R1IN, RDSIN, DS);
  and and_8 (R0IN, RDSIN, not_3_out);
  or or_1 (R1OUT, and_3_out, and_4_out);
  or or_2 (R0OUT, and_5_out, and_6_out);
  assign {controlled_buffer_1_out_2, controlled_buffer_1_out} = ONE ? 8'h1 : 8'bz;  // Controlled_Buffer controlled_buffer_7
  state state_1 (
    .OPCODE(IR[7:4]), .clock(CLK), .PCOUT(PCOUT), .PCIN(PCIN), .IRIN(IRIN), .IROUT(IROUT), .RDSIN(RDSIN),
    .RDSOUT(RDSOUT), .RSOUT(RSOUT), .MDROUT(MDROUT), .MARIN(MARIN), .ZIN(ZIN), .ZOUT(Zout), .XIN(XIN),
    .ONE(ONE), .ALU0(ALU0), .ALU1(ALU1), .OFFSET(OFFSET), .READ(READ));

  // Other names for the same wires on the sheet: S = IR[2]; IR[3] = DS; OPCODE[3:0] = IR[7:4]; R0[7:0] = print_R0;
  //   R1[7:0] = print_R1
endmodule

module ALU (
  input  [7:0] A,
  input  [7:0] B,
  input  ALU0,
  input  ALU1,
  output [7:0] z
);

  wire [7:0] adder_1_out, multiplier_1_out, nand_1_out, subtractor_1_out;

  Adder adder_1 (.a(A), .b(B), .out(adder_1_out));  // open: cin, cout
  Multiplier multiplier_1 (.a(A), .b(B), .out(multiplier_1_out));  // open: cin, cout
  Subtractor subtractor_1 (.a(A), .b(B), .out(subtractor_1_out));  // open: bin, bout
  assign nand_1_out = ~(A & B);  // NAND_Gate nand_1, 8 bits wide
  Multiplexer #(.enable("false"), .select(2), .width(8)) multiplexer_1 (
    .in0(nand_1_out), .in1(subtractor_1_out), .in2(multiplier_1_out), .in3(adder_1_out), .out(z));  // open: sel
endmodule

module state (
  input  [3:0] OPCODE,
  input  clock,
  output PCOUT,
  output PCIN,
  output IRIN,
  output IROUT,
  output RDSIN,
  output RDSOUT,
  output RSOUT,
  output MDROUT,
  output MARIN,
  output ZIN,
  output ZOUT,
  output XIN,
  output ONE,
  output ALU0,
  output ALU1,
  output OFFSET,
  output READ
);

  wire and_1_out, and_2_out, and_3_out, and_4_out, and_5_out, and_6_out, and_7_out, and_8_out, and_9_out,
       and_10_out, and_11_out, and_12_out, and_13_out, and_14_out, and_15_out, and_16_out, and_17_out,
       and_18_out, and_19_out, and_20_out, and_21_out, and_22_out, and_23_out, and_24_out, and_25_out,
       and_26_out, d_ff_1_q, d_ff_1_qn, d_ff_2_q, d_ff_2_qn, d_ff_3_q, d_ff_3_qn, d_ff_4_q, d_ff_4_qn, D_out,
       F_out, G_out, H_out, I_out, K_out, M_out, N_out, not_1_out, not_2_out, not_3_out, not_4_out, or_1_out,
       or_2_out, or_3_out, or_4_out;

  not not_1 (not_1_out, OPCODE[3]);
  not not_2 (not_2_out, OPCODE[2]);
  not not_3 (not_3_out, OPCODE[1]);
  not not_4 (not_4_out, OPCODE[0]);
  and and_1 (and_1_out, d_ff_1_qn, d_ff_2_q, d_ff_4_q, OPCODE[3], OPCODE[2], OPCODE[1], OPCODE[0]);
  and and_2 (and_2_out, d_ff_1_qn, d_ff_2_q, d_ff_3_q, d_ff_4_q);
  and and_3 (and_3_out, d_ff_2_q, d_ff_3_q, d_ff_4_q, OPCODE[0]);
  and and_4 (and_4_out, d_ff_2_q, d_ff_3_q, d_ff_4_q, OPCODE[1]);
  and and_5 (and_5_out, d_ff_2_q, d_ff_3_q, d_ff_4_q, OPCODE[2]);
  and and_6 (and_6_out, d_ff_1_q, d_ff_2_q, d_ff_3_qn, d_ff_4_qn);
  and and_7 (and_7_out, d_ff_1_qn, d_ff_3_qn);
  and and_8 (and_8_out, d_ff_1_qn, d_ff_2_q, d_ff_4_q);
  and and_9 (and_9_out, d_ff_1_q, d_ff_2_q, d_ff_3_q, d_ff_4_qn);
  and and_10 (and_10_out, d_ff_1_q, d_ff_2_q, d_ff_3_q, not_3_out, OPCODE[0]);
  and and_11 (and_11_out, d_ff_1_q, d_ff_2_q, d_ff_3_q, OPCODE[1], not_4_out);
  and and_12 (and_12_out, d_ff_2_qn, d_ff_3_q, d_ff_4_q);
  and and_13 (and_13_out, d_ff_2_q, d_ff_3_qn, d_ff_4_q, not_1_out);
  and and_14 (and_14_out, d_ff_2_q, d_ff_3_qn, d_ff_4_q, not_2_out);
  and and_15 (and_15_out, d_ff_2_q, d_ff_3_qn, d_ff_4_q, not_3_out);
  and and_16 (and_16_out, d_ff_2_q, d_ff_4_q, not_4_out);
  and and_17 (and_17_out, d_ff_1_qn, d_ff_2_q, d_ff_3_q);
  and and_18 (and_18_out, d_ff_1_q, d_ff_4_q, OPCODE[1]);
  and and_19 (and_19_out, d_ff_1_q, d_ff_3_q, d_ff_4_qn);
  and and_20 (and_20_out, d_ff_1_qn, d_ff_2_q, d_ff_3_qn, d_ff_4_qn);
  and and_21 (and_21_out, d_ff_1_qn, d_ff_2_q, d_ff_3_qn, not_1_out);
  and and_22 (and_22_out, d_ff_1_qn, d_ff_2_q, d_ff_3_qn, not_2_out);
  and and_23 (and_23_out, d_ff_1_qn, d_ff_2_q, d_ff_3_qn, not_3_out);
  and and_24 (and_24_out, d_ff_1_qn, d_ff_2_q, d_ff_4_q, not_4_out);
  and and_25 (and_25_out, d_ff_2_q, d_ff_3_q, d_ff_4_q, not_2_out, not_3_out);
  and and_26 (and_26_out, d_ff_2_q, d_ff_3_q, d_ff_4_q, OPCODE[0]);
  or or_1 (or_1_out, and_1_out, and_2_out, and_3_out, and_4_out, and_5_out, and_6_out);
  or or_2 (or_2_out, and_7_out, and_8_out, and_9_out, and_10_out, and_11_out);
  or or_3 (or_3_out, and_12_out, and_13_out, and_14_out, and_15_out, and_16_out, and_17_out, and_18_out, and_19_out);
  or or_4 (or_4_out, and_20_out, and_21_out, and_22_out, and_23_out, and_24_out, and_25_out, and_26_out);
  D_Flip_Flop d_ff_1 (.D(or_1_out), .clk(clock), .Q(d_ff_1_q), .Qn(d_ff_1_qn));  // open: preset, reset
  D_Flip_Flop d_ff_2 (.D(or_2_out), .clk(clock), .Q(d_ff_2_q), .Qn(d_ff_2_qn));  // open: preset, reset
  D_Flip_Flop d_ff_3 (.D(or_3_out), .clk(clock), .Q(d_ff_3_q), .Qn(d_ff_3_qn));  // open: preset, reset
  D_Flip_Flop d_ff_4 (.D(or_4_out), .clk(clock), .Q(d_ff_4_q), .Qn(d_ff_4_qn));  // open: preset, reset
  and A (PCOUT, d_ff_1_qn, d_ff_2_qn, d_ff_3_qn, d_ff_4_qn);
  and B (IRIN, d_ff_1_qn, d_ff_2_q, d_ff_3_qn, d_ff_4_qn);
  and C (ONE, d_ff_1_qn, d_ff_2_q, d_ff_3_qn, d_ff_4_q);
  and D (D_out, d_ff_1_qn, d_ff_2_q, d_ff_3_q, d_ff_4_q);
  and E (RDSOUT, d_ff_1_q, d_ff_2_q, d_ff_3_q, d_ff_4_q);
  and F (F_out, d_ff_1_q, d_ff_2_q, d_ff_3_q, d_ff_4_qn);
  and G (G_out, d_ff_1_qn, d_ff_2_qn, d_ff_3_q, d_ff_4_q);
  and H (H_out, d_ff_1_q, d_ff_2_q, d_ff_3_qn, d_ff_4_q);
  and I (I_out, d_ff_1_q, d_ff_2_qn, d_ff_3_q, d_ff_4_qn);
  and J (OFFSET, d_ff_1_q, d_ff_2_qn, d_ff_3_q, d_ff_4_q);
  and K (K_out, d_ff_1_qn, d_ff_2_q, d_ff_3_q, d_ff_4_qn);
  and M (M_out, d_ff_1_q, d_ff_2_q, d_ff_3_qn, d_ff_4_qn);
  and N (N_out, d_ff_1_q, d_ff_2_qn, d_ff_3_qn, d_ff_4_qn);
  and O (RDSIN, d_ff_1_qn, d_ff_2_qn, d_ff_3_q, d_ff_4_qn);
  or or_5 (PCIN, D_out, N_out);
  or or_6 (IROUT, M_out, OFFSET);
  or or_7 (RSOUT, G_out, H_out, I_out, F_out);
  or or_8 (MDROUT, K_out, IRIN);
  or or_9 (MARIN, PCOUT, F_out);
  or or_10 (ZIN, G_out, H_out, I_out, ONE, OFFSET, K_out, M_out);
  or or_11 (ZOUT, D_out, N_out, RDSIN);
  or or_12 (XIN, PCOUT, RDSOUT);
  or or_13 (ALU0, ONE, H_out, I_out, OFFSET, M_out, K_out);
  or or_14 (ALU1, ONE, H_out, OFFSET, K_out, M_out);
  or or_15 (READ, PCOUT, IRIN, F_out, K_out);
endmodule
